# Fritzing sketch smart_bottle (saved by Fritzing 0.9.3b)
breadboards: 1

parts:
  U1 = NodeMCU V1.0
  R1 = Resistor [tolerance=±5% resistance=10k package=THT]
  R2 = Photocell (LDR) [package=THT]
  DS1 = DS18B20 1-Wire Temperature Sensor [part_number=DS18B20]

nets:
  3V3: U1.3V3, R2.pin_1, DS1.VDD
  N1: U1.GND, R1.Pin_1, DS1.DQ
  N2: U1.D6, DS1.GND
  N3: U1.A0, R1.Pin_0, R2.pin_0

custom parts:
  NodeMCU V1.0: ESP8266 based NodeMCU
